# Fritzing sketch USBChessClock (saved by Fritzing 0.9.0b)

parts:
  Part1 = Arduino Uno (Rev3)
  S1 = Toggle Switch [package=THT]
  U1 = LCD-16X2 [package=lcd-16x2]
  LED1 = smd LED [color="Red (633nm)" package="0805 [SMD]"]
  LED2 = smd LED [color="Red (633nm)" package="0805 [SMD]"]
  R1 = TRIMPOT [package=3386u]
  J1 = Piezo Speaker
  R2 = Resistor [tolerance=±5% resistance=100 package="0805 [SMD]"]
  R3 = Resistor [tolerance=±5% resistance=220 package=THT]
  R4 = Resistor [tolerance=±5% resistance=220 package=THT]
  S4 = Pushbutton [package="[THT]"]

nets (from the breadboard view):
  GND: Part1.A5/SCL, Part1.GND, S1.L2, U1.VSS, LED1.anode, LED2.anode, J1.pin1, R2.Pin_0, S4.Pin_3, S4.Pin_4
  N1: Part1.D8, S1.L1
  N2: Part1.D9_PWM, R4.Pin_0
  N3: Part1.D10_PWM/SS, R3.Pin_0
  N4: Part1.D11_PWM/MOSI, U1.E
  N5: Part1.D12/MISO, U1.RS
  N6: Part1.D2, U1.DB7
  N7: Part1.D3_PWM, U1.DB6
  N8: Part1.D4, U1.DB5
  N9: Part1.D5_PWM, U1.DB4
  N10: Part1.D6_PWM, J1.pin2
  5V: Part1.5V, U1.VDD, U1.A, R1.CW
  N11: U1.VO, R1.WIPER
  N12: U1.K, R2.Pin_1
